# Fritzing sketch PFS Led vue schematique (saved by Fritzing 0.9.3b)
breadboards: 1

parts:
  Composant1 = Arduino Uno (Rev3)
  LED1 = LED - 5mm [color="Red (633nm)" package="5 mm [THT]"]
  LED2 = LED - 5mm [color="Red (633nm)" package="5 mm [THT]"]
  LED3 = LED - 5mm [color="Red (633nm)" package="5 mm [THT]"]
  LED4 = LED - 5mm [color="Red (633nm)" package="5 mm [THT]"]
  LED6 = LED - 5mm [color="Red (633nm)" package="5 mm [THT]"]
  LED7 = LED - 5mm [color="Red (633nm)" package="5 mm [THT]"]
  LED8 = LED - 5mm [color="Red (633nm)" package="5 mm [THT]"]
  LED9 = LED - 5mm [color="Red (633nm)" package="5 mm [THT]"]
  LED10 = LED - 5mm [color="Red (633nm)" package="5 mm [THT]"]
  LED11 = LED - 5mm [color="Red (633nm)" package="5 mm [THT]"]
  R1 = Resistor [tolerance=±5% resistance=220 package=THT]
  R2 = Resistor [tolerance=±5% resistance=220 package=THT]
  R3 = Resistor [tolerance=±5% resistance=220 package=THT]
  R5 = Resistor [tolerance=±5% resistance=220 package=THT]
  R6 = Resistor [tolerance=±5% resistance=220 package=THT]
  R7 = Resistor [tolerance=±5% resistance=220 package=THT]
  R8 = Resistor [tolerance=±5% resistance=220 package=THT]
  R9 = Resistor [tolerance=±5% resistance=220 package=THT]
  R11 = Resistor [tolerance=±5% resistance=220 package=THT]
  R12 = Resistor [tolerance=±5% resistance=220 package=THT]

nets:
  N1: Composant1.D8, R11.Pin_1
  N2: Composant1.D9_PWM, R2.Pin_1
  N3: Composant1.D10_PWM/SS, R1.Pin_1
  N4: Composant1.GND, LED1.cathode, LED2.cathode, LED3.cathode, LED4.cathode, LED6.cathode, LED7.cathode, LED8.cathode, LED9.cathode, LED10.cathode, LED11.cathode
  N5: Composant1.D1/TX, R7.Pin_0
  N6: Composant1.D2, R6.Pin_0
  N7: Composant1.D3_PWM, R5.Pin_0
  N8: Composant1.D4, R8.Pin_1
  N9: Composant1.D5_PWM, R9.Pin_1
  N10: Composant1.D6_PWM, LED10.anode, R12.Pin_0, R12.Pin_1
  N11: Composant1.D7, R3.Pin_1
  N12: LED1.anode, R9.Pin_0
  N13: LED2.anode, R8.Pin_0
  N14: LED3.anode, R7.Pin_1
  N15: LED4.anode, R11.Pin_0
  N16: LED6.anode, R1.Pin_0
  N17: LED7.anode, R2.Pin_0
  N18: LED8.anode, R6.Pin_1
  N19: LED9.anode, R5.Pin_1
  N20: LED11.anode, R3.Pin_0
