# Fritzing sketch Fritzing fini mod1 (saved by Fritzing 0.9.3b)
breadboards: 1

parts:
  Composant2 = Arduino Uno (Rev3)
  R9 = Resistor [tolerance=±5% resistance=2.2k package=THT]
  LED3 = LED - 5mm [color="Infrared (940nm)" package="5 mm [THT]"]
  R11 = Resistor [tolerance=±5% resistance=470k package=THT]
  LED4 = smd LED [color="Red (633nm)" package="0805 [SMD]"]
  R14 = PHOTOCELL [package=photocell]
  C5 = Ceramic Capacitor [capacitance=1µF package="0805 [SMD, multilayer]"]
  C6 = Ceramic Capacitor [capacitance=100nF package="0805 [SMD, multilayer]"]
  R12 = Resistor [tolerance=±5% resistance=1k package=THT]
  R15 = Resistor [tolerance=±5% resistance=22k package="0805 [SMD]"]
  IC1 = LM324 [package=dil16]
  R13 = Resistor [tolerance=±5% resistance=68k package=THT]
  R10 = Resistor [tolerance=±5% resistance=100 package=THT]

nets:
  N1: Composant2.A0, LED4.anode, R10.Pin_0
  N2: Composant2.5V, IC1.V+
  GND: Composant2.GND, LED3.cathode, LED4.cathode, R14.P$1, R12.Pin_1, IC1.GND, R13.Pin_1
  N3: R9.Pin_0, LED3.anode
  N4: R9.Pin_1, R15.Pin_1
  N5: R11.Pin_0, C6.1, R12.Pin_0, IC1.IN2-
  N6: R11.Pin_1, C6.0, IC1.OUT2, R10.Pin_1
  N7: R14.P$2, C5.1, R15.Pin_0
  N8: C5.0, IC1.IN2+, R13.Pin_0

custom parts:
  LM324: LM324 Quad OpAmp

// code stored in the sketch: Untitled.ino

