# Fritzing sketch PFS final (saved by Fritzing 0.9.3b)
breadboards: 1

parts:
  Composant1 = Arduino Uno (Rev3)
  R1 = Resistor [tolerance=±5% resistance=220 package=THT]
  R2 = Resistor [tolerance=±5% resistance=220 package=THT]
  R3 = Resistor [tolerance=±5% resistance=220 package=THT]
  R4 = Resistor [tolerance=±5% resistance=220 package=THT]
  R5 = Resistor [tolerance=±5% resistance=220 package=THT]
  R6 = Resistor [tolerance=±5% resistance=220 package=THT]
  R7 = Resistor [tolerance=±5% resistance=220 package=THT]
  R8 = Resistor [tolerance=±5% resistance=220 package=THT]
  R9 = Resistor [tolerance=±5% resistance=220 package=THT]
  R10 = Resistor [tolerance=±5% resistance=220 package=THT]
  LED1 = LED - 5mm [color="Red (633nm)" package="5 mm [THT]"]
  LED2 = LED - 5mm [color="Red (633nm)" package="5 mm [THT]"]
  LED3 = LED - 5mm [color="Red (633nm)" package="5 mm [THT]"]
  LED4 = LED - 5mm [color="Red (633nm)" package="5 mm [THT]"]
  LED5 = LED - 5mm [color="Red (633nm)" package="5 mm [THT]"]
  LED6 = LED - 5mm [color="Red (633nm)" package="5 mm [THT]"]
  LED7 = LED - 5mm [color="Red (633nm)" package="5 mm [THT]"]
  LED8 = LED - 5mm [color="Red (633nm)" package="5 mm [THT]"]
  LED9 = LED - 5mm [color="Red (633nm)" package="5 mm [THT]"]
  LED10 = LED - 5mm [color="Red (633nm)" package="5 mm [THT]"]

nets:
  N1: Composant1.D8, R3.Pin_1
  N2: Composant1.D9_PWM, R2.Pin_1
  N3: Composant1.D10_PWM/SS, R1.Pin_1
  N4: Composant1.D1/TX, R10.Pin_1
  N5: Composant1.D2, R9.Pin_1
  N6: Composant1.D3_PWM, R8.Pin_1
  N7: Composant1.D4, R7.Pin_1
  N8: Composant1.D5_PWM, R6.Pin_1
  N9: Composant1.D6_PWM, R5.Pin_1
  N10: Composant1.D7, R4.Pin_1
  N11: Composant1.GND, LED1.cathode, LED2.cathode, LED3.cathode, LED4.cathode, LED5.cathode, LED6.cathode, LED7.cathode, LED8.cathode, LED9.cathode, LED10.cathode
  N12: R1.Pin_0, LED9.anode
  N13: R2.Pin_0, LED10.anode
  N14: R3.Pin_0, LED8.anode
  N15: R4.Pin_0, LED7.anode
  N16: R5.Pin_0, LED6.anode
  N17: R6.Pin_0, LED5.anode
  N18: R7.Pin_0, LED4.anode
  N19: R8.Pin_0, LED2.anode
  N20: R9.Pin_0, LED3.anode
  N21: R10.Pin_0, LED1.anode
