# Fritzing sketch Schéma base mod1 (saved by Fritzing 0.9.3b)
breadboards: 1

parts:
  Composant2 = Arduino Uno (Rev3)
  U2 = LM124-324 Quad Opamp [package="DIP (Dual Inline)"]
  R8 = Resistor [tolerance=±5% resistance=2.2k package=THT]
  R9 = Resistor [tolerance=±5% resistance=2.2k package=THT]
  LED3 = LED - 5mm [color="Infrared (940nm)" package="5 mm [THT]"]
  R10 = Resistor [tolerance=±5% resistance=100 package=THT]
  R11 = Resistor [tolerance=±5% resistance=470 package=THT]
  R12 = Resistor [tolerance=±5% resistance=1k package=THT]
  R13 = Resistor [tolerance=±5% resistance=68k package=THT]
  LED4 = smd LED [color="Red (633nm)" package="0805 [SMD]"]
  R14 = PHOTOCELL [package=photocell]
  C5 = Ceramic Capacitor [capacitance=1µF package="0805 [SMD, multilayer]"]
  C6 = Ceramic Capacitor [capacitance=100nF package="0805 [SMD, multilayer]"]

nets (from the schematic view):
  N1: Composant2.A0, R10.Pin_0
  N2: Composant2.5V, U2.VCC+, R8.Pin_1, R9.Pin_1
  N3: Composant2.GND, U2.VCC-, LED3.cathode, R12.Pin_1, R13.Pin_1, LED4.cathode, R14.P$1
  N4: U2.2IN+, R13.Pin_0, C5.0
  N5: U2.2IN-, R11.Pin_0, R12.Pin_0, C6.1
  N6: U2.2OUT, R10.Pin_1
  N7: R8.Pin_0, R14.P$2, C5.1
  N8: R9.Pin_0, LED3.anode
  N9: R11.Pin_1, C6.0

// code stored in the sketch: Untitled.ino

